# Fritzing sketch lcd (saved by Fritzing 0.9.3b)
breadboards: 1

parts:
  LCD1 = LCD screen
  Composant1 = Arduino Uno (Rev3)
  R1 = Trimmer Potentiometer [maximum_resistance=10kΩ package=THT]

nets:
  VSS: LCD1.VSS, LCD1.R/W, LCD1.LED-, Composant1.GND, R1.leg1
  VDD: LCD1.VDD, LCD1.LED+, Composant1.5V, R1.leg2
  N1: LCD1.V0, R1.wiper
  N2: LCD1.RS, Composant1.D12/MISO
  N3: LCD1.E, Composant1.D11_PWM/MOSI
  N4: LCD1.DB4, Composant1.D5_PWM
  N5: LCD1.DB5, Composant1.D4
  N6: LCD1.DB6, Composant1.D3_PWM
  N7: LCD1.DB7, Composant1.D2
